# Fritzing sketch morseShematic (saved by Fritzing 1.0.1rc)
breadboards: 1

parts:
  Part1 = Arduino Uno (Rev3)
  S1 = Pushbutton [package="[THT]"]
  R1 = Resistor [tolerance=±5% power=0.25 resistance=220 package=THT]
  DI1 = 7-Segment LED Display [package=THT]
  R2 = Resistor [tolerance=±5% power=0.25 resistance=220 package=THT]

nets:
  N1: Part1.A0, S1.Pin_1, S1.Pin_2, R1.Pin_0
  N2: Part1.D8, DI1.cathodeD
  N3: Part1.D9_PWM, DI1.cathodeE
  N4: Part1.D2, DI1.cathodeB
  N5: Part1.D3_PWM, DI1.cathodeA
  N6: Part1.D4, DI1.cathodeF
  N7: Part1.D5_PWM, DI1.cathodeG
  N8: Part1.D6_PWM, DI1.cathodeDP
  N9: Part1.D7, DI1.cathodeC
  N10: Part1.5V, R1.Pin_1
  N11: Part1.GND, S1.Pin_3, S1.Pin_4, R2.Pin_1
  N12: DI1.commAnode#2, R2.Pin_0
